// Logisim project proj1.circ as structural Verilog: 1 circuit, main circuit main
module main (
  input  A,
  input  B,
  input  C,
  output F
);

  wire and_1_out, and_2_out, CLK_out, not_1_out, PWR_out, RES_out;

  Button CLK (.out(CLK_out));
  not not_1 (not_1_out, B);
  and and_1 (and_1_out, A, not_1_out);
  and and_2 (and_2_out, B, C);
  or or_1 (F, and_1_out, and_2_out);
  Button #(.press("passive")) PWR (.out(PWR_out));
  Button RES (.out(RES_out));
  // Digital_Oscilloscope #(.frontlines("falling"), .nState(8)) digital_oscilloscope_1: pin names not known; wires that end beside it: CLK_out, A, B, C, F, PWR_out, RES_out
endmodule
